# Fritzing sketch thermostat (saved by Fritzing 0.9.3b)
breadboards: 1

parts:
  LCD1 = LCD screen
  Part1 = Arduino Uno (Rev3)
  Part2 = Real Time Clock Module - DS1307 RTC Breakout Board
  R1 = Resistor [tolerance=±1% resistance=3k package=THT]
  R2 = Resistor [tolerance=±1% resistance=330 package=THT]
  R3 = Resistor [tolerance=±1% resistance=3k package=THT]
  LED1 = LED - 3mm [color="Red (633nm)" package="3 mm [THT]"]

nets:
  N1: LCD1.V0, R1.Pin_0
  N2: LCD1.RS, Part1.D12/MISO
  GND: LCD1.R/W, LCD1.LED-, Part1.GND, Part2.GND, R1.Pin_1, R3.Pin_0
  N3: LCD1.E, LCD1.DB0, Part1.D11_PWM/MOSI
  N4: LCD1.DB4, Part1.D5_PWM
  N5: LCD1.DB5, Part1.D4
  N6: LCD1.DB6, Part1.D3_PWM
  N7: LCD1.DB7, Part1.D2
  N8: LCD1.LED+, R2.Pin_0
  N9: Part1.A4/SDA, Part2.SDA
  N10: Part1.A5/SCL, Part2.SCL
  N11: Part1.D8, LED1.anode
  5V: Part1.5V, Part2.5V, R2.Pin_1
  N12: R3.Pin_1, LED1.cathode
